// Logisim project PipelinedProcessor.circ as structural Verilog: 7 circuits, main circuit main
module main (
);

  wire _0, and_1_out, and_2_out, and_5_out, and_6_out, and_7_out, and_8_out, and_9_out, and_10_out,
       and_11_out, and_12_out, ANY, BEQ_MEM, BEQ_WB, BranchMUX, Clk, comparator_1_eq, comparator_2_eq,
       comparator_3_eq, comparator_4_eq, comparator_5_eq, comparator_6_eq, isBEQ, isJALR, JALR_MEM, JALR_WB,
       NOP, or_3_out, or_4_out, or_5_out, or_6_out, or_7_out, or_8_out, or_9_out, or_10_out, PC_En, RAMSel,
       register_1_q, Res, ResultSel, Sel, SelectID1, SelectID2, STALL, Str, WBSel, WrEN;
  wire [1:0] FUNC, priority_encoder_1_out, priority_encoder_2_out;
  wire [3:0] EXROM, IDROM, MEMROM, ReadRegNO1, ReadRegNO2, Rx, Rx_EX, Rx_MEM, Rx_WB, Ry, Rz, WBROM;
  wire [19:0] OFF_ID_RR;
  wire [31:0] A_DI, adder_1_out, adder_2_out, ADR, alu_1_out, B_DI, DATA, EX____MEM_sr_2,
       ID_RR____EX_offset_2, ID_RR____EX_pc_2, ID_RR____EX_ry_2, ID_RR____EX_rz_2, IF____ID_RR_pc_out, INPUT,
       MEM____WB_mem_2, MEM____WB_result_2, multiplexer_3_out, multiplexer_4_out, multiplexer_5_out,
       multiplexer_6_out, multiplexer_7_out, OUT1, OUT2, PC_q, ram_1_data, ram_2_data, Result_EX, Result_MEM;

  Clock clock_1 (.out(Clk));
  Button button_1 (.out(Res));
  Register #(.width(1)) register_1 (.D(isBEQ), .Q(register_1_q), .clk(Clk));  // open: en, clr
  and and_1 (and_1_out, isBEQ, _0);
  Multiplexer #(.width(4), .enable("false")) multiplexer_1 (.in0(Rx), .in1(Ry), .out(ReadRegNO1), .sel(SelectID1));
  Multiplexer #(.width(4), .enable("false")) multiplexer_2 (.in0(Ry), .in1(Rz), .out(ReadRegNO2), .sel(SelectID2));
  Multiplexer #(.select(2), .width(32), .enable("false")) multiplexer_3 (
    .in0(adder_1_out), .in1(multiplexer_4_out), .out(multiplexer_3_out), .sel({isJALR, isBEQ}));  // open: in2, in3
  Register #(.width(32)) PC (.D(multiplexer_3_out), .en(PC_En), .Q(PC_q), .clk(Clk), .clr(Res));
  and and_2 (and_2_out, STALL, ~register_1_q);  // AND_Gate
  or or_1 (NOP, isJALR, and_1_out);
  or or_2 (ANY, isBEQ, BEQ_MEM, BEQ_WB, isJALR, JALR_MEM, JALR_WB);
  Multiplexer #(.width(32), .enable("false")) multiplexer_4 (
    .in0(adder_1_out), .in1(adder_2_out), .out(multiplexer_4_out), .sel(BranchMUX));
  Adder #(.width(32)) adder_1 (.a(PC_q), .b(32'h1), .out(adder_1_out));  // open: cin, cout
  and and_3 (PC_En, 1'b1, ~and_2_out);  // AND_Gate
  and and_4 (BranchMUX, _0, isBEQ);
  Multiplexer #(.width(32), .enable("false")) multiplexer_5 (
    .in0(adder_1_out), .in1({32{1'b0}}), .out(multiplexer_5_out), .sel(STALL));
  RAM #(.addrWidth(24), .dataWidth(32)) ram_1 (
    .addr(PC_q[23:0]), .data(ram_1_data), .clk(Clk), .ld(1'b1));  // open: sel, clr
  Multiplexer #(.width(32), .enable("false")) multiplexer_6 (
    .in0(ram_1_data), .in1(32'h70000000), .out(multiplexer_6_out), .sel(STALL));
  IF_IDRR_Buffer IF____ID_RR (
    .PC_In(multiplexer_5_out), .Instruction_In(multiplexer_6_out), .PC_Out(IF____ID_RR_pc_out), .Clk(Clk),
    .RZ(Rz), .RY(Ry), .RX(Rx), .Opcode(IDROM), .OFFSET(OFF_ID_RR), .NOP(NOP));
  or or_3 (or_3_out, isJALR, isBEQ);
  ROM #(.addrWidth(4), .dataWidth(3)) rom_1 (.addr(IDROM), .data({STALL, SelectID2, SelectID1}));  // open: sel
  or or_4 (or_4_out, BEQ_WB, JALR_WB);
  Comparator #(.width(4)) comparator_1 (.a(ReadRegNO2), .b(Rx_EX), .eq(comparator_1_eq));  // open: gt, lt
  Comparator #(.width(4)) comparator_2 (.a(ReadRegNO2), .b(Rx_MEM), .eq(comparator_2_eq));  // open: gt, lt
  or or_5 (or_5_out, BEQ_MEM, JALR_MEM);
  Comparator #(.width(4)) comparator_3 (.a(ReadRegNO2), .b(Rx_WB), .eq(comparator_3_eq));  // open: gt, lt
  or or_6 (or_6_out, BEQ_WB, JALR_WB);
  Comparator #(.width(4)) comparator_4 (.a(ReadRegNO1), .b(Rx_EX), .eq(comparator_4_eq));  // open: gt, lt
  or or_7 (or_7_out, isJALR, isBEQ);
  Comparator #(.width(4)) comparator_5 (.a(ReadRegNO1), .b(Rx_MEM), .eq(comparator_5_eq));  // open: gt, lt
  or or_8 (or_8_out, BEQ_MEM, JALR_MEM);
  Comparator #(.width(4)) comparator_6 (.a(ReadRegNO1), .b(Rx_WB), .eq(comparator_6_eq));  // open: gt, lt
  and and_5 (and_5_out, ~comparator_1_eq, ~comparator_2_eq, ~comparator_3_eq);  // AND_Gate
  Dual_Ported_Register_File dual_ported_register_file_1 (
    .CLK(Clk), .WrREGNO(Rx_WB), .RdREGNO1(ReadRegNO1), .RdREGNO2(ReadRegNO2), .INPUT(INPUT), .OUT1(OUT1),
    .OUT2(OUT2), .WrEN(WrEN));
  and and_6 (and_6_out, ~comparator_4_eq, ~comparator_5_eq, ~comparator_6_eq);  // AND_Gate
  or or_9 (or_9_out, and_6_out, ANY);
  and and_7 (and_7_out, ~or_7_out, comparator_4_eq);  // AND_Gate
  and and_8 (and_8_out, comparator_5_eq, ~or_8_out, ~comparator_4_eq);  // AND_Gate
  and and_9 (and_9_out, comparator_6_eq, ~or_4_out, ~comparator_4_eq, comparator_5_eq);  // AND_Gate
  or or_10 (or_10_out, and_5_out, ANY);
  and and_10 (and_10_out, ~or_3_out, comparator_1_eq);  // AND_Gate
  and and_11 (and_11_out, comparator_2_eq, ~or_5_out, ~comparator_1_eq);  // AND_Gate
  and and_12 (and_12_out, comparator_3_eq, ~or_6_out, ~comparator_1_eq, comparator_2_eq);  // AND_Gate
  IDRR_EX_Buffer ID_RR____EX (
    .PC(IF____ID_RR_pc_out), .OP(IDROM), .RY(A_DI), .RZ(B_DI), .RX(Rx), .OFFSET(OFF_ID_RR),
    .PC_2(ID_RR____EX_pc_2), .OP_2(EXROM), .RY_2(ID_RR____EX_ry_2), .RZ_2(ID_RR____EX_rz_2), .RX_2(Rx_EX),
    .OFFSET_2(ID_RR____EX_offset_2), .in_7(Clk));  // open: in_8
  Priority_Encoder #(.select(2)) priority_encoder_1 (
    .in0(or_9_out), .in1(and_7_out), .in2(and_8_out), .in3(and_9_out), .out(priority_encoder_1_out));  // open: gs, en_out, en_in
  Priority_Encoder #(.select(2)) priority_encoder_2 (
    .in0(or_10_out), .in1(and_10_out), .in2(and_11_out), .in3(and_12_out), .out(priority_encoder_2_out));  // open: gs, en_out, en_in
  Multiplexer #(.width(32), .enable("false")) multiplexer_7 (
    .in0(ID_RR____EX_rz_2), .in1(ID_RR____EX_offset_2), .out(multiplexer_7_out), .sel(Sel));
  Multiplexer #(.select(2), .width(32), .enable("false")) multiplexer_8 (
    .in0(OUT2), .in1(Result_EX), .in2(Result_MEM), .in3(DATA), .out(B_DI), .sel(priority_encoder_2_out));
  Adder #(.width(32)) adder_2 (.a(ID_RR____EX_pc_2), .b(ID_RR____EX_offset_2), .out(adder_2_out));  // open: cin, cout
  Multiplexer #(.select(2), .width(32), .enable("false")) multiplexer_9 (
    .in0(OUT1), .in1(Result_EX), .in2(Result_MEM), .in3(DATA), .out(A_DI), .sel(priority_encoder_1_out));
  ALU alu_1 (.FUNC(FUNC), .A(ID_RR____EX_ry_2), .B(multiplexer_7_out), .OUT(alu_1_out));
  ROM #(.addrWidth(4), .dataWidth(6)) rom_2 (.addr(EXROM), .data({isJALR, isBEQ, ResultSel, Sel, FUNC}));  // open: sel
  Multiplexer #(.width(32), .enable("false")) multiplexer_10 (
    .in0(adder_2_out), .in1(alu_1_out), .out(Result_EX), .sel(ResultSel));
  Comparator #(.width(32)) comparator_7 (.a({32{1'b0}}), .b(alu_1_out), .eq(_0));  // open: gt, lt
  EX_MEM_Buffer EX____MEM (
    .OP(EXROM), .RX(Rx_EX), .ADR(adder_2_out), .Result(Result_EX), .SR(ID_RR____EX_rz_2), .CLK(Clk),
    .OP_2(MEMROM), .RX_2(Rx_MEM), .ADR_2(ADR), .Result_2(Result_MEM), .SR_2(EX____MEM_sr_2), .Res(Res));
  RAM #(.addrWidth(24), .dataWidth(32), .bus("separate")) ram_2 (
    .addr(Result_MEM[23:0]), .din(EX____MEM_sr_2), .data(ram_2_data), .str(Str), .sel(RAMSel), .ld(1'b1));  // open: clk, clr
  ROM #(.addrWidth(4), .dataWidth(4)) rom_3 (.addr(MEMROM), .data({JALR_MEM, BEQ_MEM, Str, RAMSel}));  // open: sel
  MEM_WB_Buffer MEM____WB (
    .OP(MEMROM), .RX(Rx_MEM), .MEM(ram_2_data), .Result(Result_MEM), .in_6(Clk), .OP_2(WBROM), .RX_2(Rx_WB),
    .MEM_2(MEM____WB_mem_2), .Result_2(MEM____WB_result_2), .Res(Res));
  Multiplexer #(.width(32), .enable("false")) multiplexer_11 (
    .in0(MEM____WB_mem_2), .in1(MEM____WB_result_2), .out(INPUT), .sel(WBSel));
  ROM #(.addrWidth(4), .dataWidth(4)) rom_4 (.addr(WBROM), .data({JALR_WB, BEQ_WB, WrEN, WBSel}));  // open: sel

  // Other names for the same wires on the sheet: PCSrc[1:0] = {isJALR, isBEQ}; Wr_RX[3:0] = Rx_WB

  // Notes on the sheet:
  //   Any BEQ or JALR?
  //   Do we set the PC to stop incrementing or not during BEQ
  //   NOP due to JALR or BEQ
  //   Register Read selection depending on type of instruction
  //   Instruction Decode Rom
  //   contents of rom_1 (hex, n*v repeats v):
  //   3 3 3 0 0 4 4
  //   LC-2200 PIPELINE
  //   LUKA ANTOLIC_SOBAN
  //   Forwarding Unit
  //   Execute Rom
  //   contents of rom_2 (hex, n*v repeats v):
  //   8 9 c 4 4 12
  //   Memory ROM
  //   contents of rom_3 (hex, n*v repeats v):
  //   0 0 0 1 3 4 8
  //   WriteBack ROM
  //   contents of rom_4 (hex, n*v repeats v):
  //   3 3 3 2 2 4 8
endmodule

module Dual_Ported_Register_File (
  input  CLK,
  input  WrEN,
  input  [3:0] WrREGNO,
  input  [3:0] RdREGNO1,
  input  [3:0] RdREGNO2,
  input  [31:0] INPUT,
  output [31:0] OUT1,
  output [31:0] OUT2
);

  wire En_a0, En_a1, En_a2, En_a3, En_a4, En_at, En_fp, En_k0, En_ra, En_s0, En_s1, En_s2, En_s3, En_sp,
       En_v0;
  wire [31:0] a0, a1, a2, a3, a4, at, fp, k0, ra, s0, s1, s2, s3, sp, v0, zero;

  Decoder #(.select(4), .disabled(0)) decoder_1 (
    .out1(En_at), .out2(En_v0), .out3(En_a0), .out4(En_a1), .out5(En_a2), .out6(En_a3), .out7(En_a4),
    .out8(En_s0), .out9(En_s1), .out10(En_s2), .out11(En_s3), .out12(En_k0), .out13(En_sp), .out14(En_fp),
    .out15(En_ra), .sel(WrREGNO), .en(WrEN));  // open: out0
  Register #(.width(32)) u_zero (.D(INPUT), .en(1'b0), .Q(zero), .clk(CLK));  // open: clr
  Register #(.width(32)) u_at (.D(INPUT), .en(En_at), .Q(at), .clk(CLK));  // open: clr
  Register #(.width(32)) u_v0 (.D(INPUT), .en(En_v0), .Q(v0), .clk(CLK));  // open: clr
  Register #(.width(32)) u_a0 (.D(INPUT), .en(En_a0), .Q(a0), .clk(CLK));  // open: clr
  Register #(.width(32)) u_a1 (.D(INPUT), .en(En_a1), .Q(a1), .clk(CLK));  // open: clr
  Register #(.width(32)) u_a2 (.D(INPUT), .en(En_a2), .Q(a2), .clk(CLK));  // open: clr
  Register #(.width(32)) u_a3 (.D(INPUT), .en(En_a3), .Q(a3), .clk(CLK));  // open: clr
  Register #(.width(32)) u_a4 (.D(INPUT), .en(En_a4), .Q(a4), .clk(CLK));  // open: clr
  Multiplexer #(.select(4), .width(32), .disabled(0), .enable("false")) multiplexer_1 (
    .in0(zero), .in1(at), .in2(v0), .in3(a0), .in4(a1), .in5(a2), .in6(a3), .in7(a4), .in8(s0), .in9(s1),
    .in10(s2), .in11(s3), .in12(k0), .in13(sp), .in14(fp), .in15(ra), .out(OUT2), .sel(RdREGNO2));
  Register #(.width(32)) u_s0 (.D(INPUT), .en(En_s0), .Q(s0), .clk(CLK));  // open: clr
  Register #(.width(32)) u_s1 (.D(INPUT), .en(En_s1), .Q(s1), .clk(CLK));  // open: clr
  Register #(.width(32)) u_s2 (.D(INPUT), .en(En_s2), .Q(s2), .clk(CLK));  // open: clr
  Register #(.width(32)) u_s3 (.D(INPUT), .en(En_s3), .Q(s3), .clk(CLK));  // open: clr
  Register #(.width(32)) u_k0 (.D(INPUT), .en(En_k0), .Q(k0), .clk(CLK));  // open: clr
  Register #(.width(32)) u_sp (.D(INPUT), .en(En_sp), .Q(sp), .clk(CLK));  // open: clr
  Register #(.width(32)) u_fp (.D(INPUT), .en(En_fp), .Q(fp), .clk(CLK));  // open: clr
  Register #(.width(32)) u_ra (.D(INPUT), .en(En_ra), .Q(ra), .clk(CLK));  // open: clr
  Multiplexer #(.select(4), .width(32), .disabled(0), .enable("false")) multiplexer_2 (
    .in0(zero), .in1(at), .in2(v0), .in3(a0), .in4(a1), .in5(a2), .in6(a3), .in7(a4), .in8(s0), .in9(s1),
    .in10(s2), .in11(s3), .in12(k0), .in13(sp), .in14(fp), .in15(ra), .out(OUT1), .sel(RdREGNO1));

  // Notes on the sheet:
  //   MODIFY AT YOUR OWN RISK
endmodule

module IF_IDRR_Buffer (
  input  [31:0] PC_In,
  input  [31:0] Instruction_In,
  input  Clk,
  input  NOP,
  output [19:0] OFFSET,
  output [31:0] PC_Out,
  output [3:0] RZ,
  output [3:0] RY,
  output [3:0] RX,
  output [3:0] Opcode
);

  Register #(.width(32)) register_1 (.D(PC_In), .Q(PC_Out), .clk(Clk), .clr(NOP));  // open: en
  Register #(.width(32)) register_2 (
    .D(Instruction_In), .Q({Opcode, RX, RY, OFFSET}), .clk(Clk), .clr(NOP));  // open: en

  assign RZ = OFFSET[3:0];

  // Other names for the same wires on the sheet: OFFSET_t[15:0] = OFFSET[19:4]
endmodule

module IDRR_EX_Buffer (
  input  [31:0] PC,
  input  [3:0] OP,
  input  [31:0] RY,
  input  [31:0] RZ,
  input  [3:0] RX,
  input  [19:0] OFFSET,
  input  in_7,
  input  in_8,
  output [31:0] PC_2,
  output [3:0] OP_2,
  output [31:0] RY_2,
  output [31:0] RZ_2,
  output [3:0] RX_2,
  output [31:0] OFFSET_2
);

  wire [19:0] OFFSET_q;

  Register #(.width(32)) u_PC (.D(PC), .Q(PC_2), .clk(in_7), .clr(in_8));  // open: en
  Register #(.width(4)) OPCODE (.D(OP), .Q(OP_2), .clk(in_7), .clr(in_8));  // open: en
  Register #(.width(32)) SR1 (.D(RY), .Q(RY_2), .clk(in_7), .clr(in_8));  // open: en
  Register #(.width(32)) SR2 (.D(RZ), .Q(RZ_2), .clk(in_7), .clr(in_8));  // open: en
  Register #(.width(4)) DR (.D(RX), .Q(RX_2), .clk(in_7), .clr(in_8));  // open: en
  Register #(.width(20)) u_OFFSET (.D(OFFSET), .Q(OFFSET_q), .clk(in_7), .clr(in_8));  // open: en
  assign OFFSET_2 = {{12{OFFSET_q[19]}}, OFFSET_q};  // Bit_Extender bit_extender_1

  // Other names for the same wires on the sheet: CLK = in_7; RES = in_8
endmodule

module EX_MEM_Buffer (
  input  [3:0] OP,
  input  [3:0] RX,
  input  [31:0] ADR,
  input  [31:0] Result,
  input  [31:0] SR,
  input  Res,
  input  CLK,
  output [3:0] OP_2,
  output [3:0] RX_2,
  output [31:0] ADR_2,
  output [31:0] Result_2,
  output [31:0] SR_2
);

  Register #(.width(4)) register_1 (.D(OP), .Q(OP_2), .clk(CLK), .clr(Res));  // open: en
  Register #(.width(4)) register_2 (.D(RX), .Q(RX_2), .clk(CLK), .clr(Res));  // open: en
  Register #(.width(32)) register_3 (.D(ADR), .Q(ADR_2), .clk(CLK), .clr(Res));  // open: en
  Register #(.width(32)) register_4 (.D(Result), .Q(Result_2), .clk(CLK), .clr(Res));  // open: en
  Register #(.width(32)) register_5 (.D(SR), .Q(SR_2), .clk(CLK), .clr(Res));  // open: en
endmodule

module MEM_WB_Buffer (
  input  [3:0] OP,
  input  [3:0] RX,
  input  [31:0] MEM,
  input  [31:0] Result,
  input  Res,
  input  in_6,
  output [3:0] OP_2,
  output [3:0] RX_2,
  output [31:0] MEM_2,
  output [31:0] Result_2
);

  Register #(.width(4)) register_1 (.D(OP), .Q(OP_2), .clk(in_6), .clr(Res));  // open: en
  Register #(.width(4)) u_RX (.D(RX), .Q(RX_2), .clk(in_6), .clr(Res));  // open: en
  Register #(.width(32)) register_2 (.D(MEM), .Q(MEM_2), .clk(in_6), .clr(Res));  // open: en
  Register #(.width(32)) u_Result (.D(Result), .Q(Result_2), .clk(in_6), .clr(Res));  // open: en
endmodule

module ALU (
  input  [1:0] FUNC,
  input  [31:0] A,
  input  [31:0] B,
  output [31:0] OUT
);

  wire [31:0] adder_1_out, adder_2_out, nand_1_out, subtractor_1_out;

  Adder #(.width(32)) adder_1 (.a(A), .b(B), .out(adder_1_out), .cin(1'b0));  // open: cout
  assign nand_1_out = ~(A & B);  // NAND_Gate nand_1, 32 bits wide
  Subtractor #(.width(32)) subtractor_1 (.a(A), .b(B), .out(subtractor_1_out), .bin(1'b0));  // open: bout
  Adder #(.width(32)) adder_2 (.a(A), .b({32{1'b0}}), .out(adder_2_out), .cin(1'b1));  // open: cout
  Multiplexer #(.select(2), .width(32), .disabled(0), .enable("false")) multiplexer_1 (
    .in0(adder_1_out), .in1(nand_1_out), .in2(subtractor_1_out), .in3(adder_2_out), .out(OUT), .sel(FUNC));

  // Notes on the sheet:
  //   MODIFY AT YOUR OWN RISK
endmodule
